# Fritzing sketch MedicNestMS (saved by Fritzing 1.0.4)
breadboards: 1

parts:
  LED1 = RGB LED (com. cathode, rbg) [color="Red (633nm)" current=0.030A package="5 mm [THT]"]
  DHT2 = DHT11 Humitidy and Temperature Sensor (3 pins)
  S1 = SWITCH-MOMENTARY-2 [package=tactile-pth-12mm]
  ZS-042_RTC1 = ZS-042 RTC Module
  OLED_I2C1 = OLED 128x64 I2C Monochrome Display
  VCC1 = Battery block 9V [internal_resistance=0.1Ω]
  J1 = Piezo Speaker
  Part1 = Arduino Nano (Rev3.0)

nets (from the schematic view):
  RED: LED1.red_anode, Part1.D5
  GND: LED1.common_cathode, DHT2.Gnd, S1.2, ZS-042_RTC1.GND, OLED_I2C1.GND, VCC1.-, J1.pin2, Part1.GND
  BLUE: LED1.blue_anode, Part1.D7
  GREEN: LED1.green_anode, Part1.D6
  5V: DHT2.Plus, ZS-042_RTC1.VCC, OLED_I2C1.VDD, Part1.5V
  DHT11: DHT2.Signal, Part1.D2
  N1: S1.1, Part1.D3
  SDA: ZS-042_RTC1.SDA, OLED_I2C1.SDA, Part1.A4
  SCL/SCK: ZS-042_RTC1.SCL, OLED_I2C1.SCK, Part1.A5
  9V: VCC1.+, Part1.VIN
  Buzzer: J1.pin1, Part1.D8

custom parts:
  DHT11 Humitidy and Temperature Sensor (3 pins): DHT11 Humidity and Temperature Sensor (3 pins).
